# Fritzing sketch rc corner scale (saved by Fritzing 0.9.3b)
breadboards: 1

parts:
  Part1 = Arduino Uno (Rev3)
  S3 = Pushbutton [package="[THT]"]
  S4 = Pushbutton [package="[THT]"]
  Part3 = HX711 Weighing Sensor Module
  Part4 = HX711 Weighing Sensor Module
  Part5 = HX711 Weighing Sensor Module
  Part6 = HX711 Weighing Sensor Module
  Part2 = LCD1602-I2C
  Load_Cell2 = Load Cell - Red/white/black/green
  Load_Cell3 = Load Cell - Red/white/black/green
  Load_Cell4 = Load Cell - Red/white/black/green
  Load_Cell5 = Load Cell - Red/white/black/green
  R1 = Resistor [tolerance=±5% resistance=220k package="2010 [SMD]"]
  R2 = Resistor [tolerance=±5% resistance=220k package="2010 [SMD]"]

nets:
  N1: Part1.A0, Part4.DO/RX
  N2: Part1.A1, Part3.DO/RX
  N3: Part1.A2, Part5.DO/RX
  N4: Part1.A3, Part6.DO/RX
  N5: Part1.A4/SDA, Part2.SDA
  N6: Part1.A5/SCL, Part2.SCL
  N7: Part1.D8, S3.Pin_3, S3.Pin_4, R1.Pin_1
  N8: Part1.D11_PWM/MOSI, S4.Pin_3, S4.Pin_4, R2.Pin_0
  GND: Part1.GND, Part2.GND, R1.Pin_0, R2.Pin_1
  N9: Part1.D2, Part4.CK/TX
  N10: Part1.D3_PWM, Part3.CK/TX
  N11: Part1.D4, Part5.CK/TX
  N12: Part1.D5_PWM, Part6.CK/TX
  VCC: Part1.5V, S3.Pin_1, S3.Pin_2, S4.Pin_1, S4.Pin_2, Part6.VCC, Part2.VCC
  N13: Part3.E+, Load_Cell3.wire1
  N14: Part3.E-, Load_Cell3.wire3
  N15: Part3.A+, Load_Cell3.wire4
  N16: Part3.A-, Load_Cell3.wire2
  N17: Part4.E+, Load_Cell2.wire1
  N18: Part4.E-, Load_Cell2.wire3
  N19: Part4.A+, Load_Cell2.wire4
  N20: Part4.A-, Load_Cell2.wire2
  N21: Part5.E+, Load_Cell4.wire1
  N22: Part5.E-, Load_Cell4.wire3
  N23: Part5.A+, Load_Cell4.wire4
  N24: Part5.A-, Load_Cell4.wire2
  N25: Part6.E+, Load_Cell5.wire1, Load_Cell5.wire2
  N26: Part6.E-, Load_Cell5.wire3
  N27: Part6.A+, Load_Cell5.wire4

notes:
  FRONT RIGHT
  FRONT LEFT
  REAR RIGHT
  REAR LEFT
  LCD i2C 16x2
  LOADCELL
  HX711
  RED
  E+
  BLACK
  E-
  WHITE
  A-
  GREEN
  A+
  B-
  B+
  TARE BUTTON
  WEIGHT BUTTON
  LOADCELL 0 - 2Kg
  FRONT RIGHT
  HX711
  ARDUINO UNO
  GND
  Ground
  DT
  A0
  SCK
  2
  VCC
  +5v
  FRONT LEFT
  HX711
  ARDUINO UNO
  GND
  Ground
  DT
  A1
  SCK
  3
  VCC
  +5v
  REAR RIGHT
  HX711
  ARDUINO UNO
  GND
  Ground
  DT
  A2
  SCK
  4
  VCC
  +5v
  REAR LEFT
  HX711
  ARDUINO UNO
  GND
  Ground
  DT
  A3
  SCK
  5
  VCC
  +5v
  Push Button
  ARDUINO UNO
  Weight Button
  8
  Tare Button
  11
  LCD
  ARDUINO UNO
  GND
  Ground
  VCC
  +5v
  SDA
  A4
  SCL
  A5

custom parts:
  LCD1602-I2C: A standard character display, usually with 2x16 characters. Comes in many colors with LCM1602 IIC attached.
  Load Cell - Red/white/black/green: A rectangle load cell/weighting pressure Sensor with four wires - Red, white, black, green. Normally corresponding with E+, E-, A+, A- respectively.
